# Fritzing sketch SelfB_PCB (saved by Fritzing 0.8.7b)
circuit board: 6.88566cm x 5.36311cm
breadboards: 1

parts:
  DRV_1 = DRV 8825 Stepper Motor Carrier, High Current [part_number="DRV 8825"]
  DRV_2 = DRV 8825 Stepper Motor Carrier, High Current [part_number="DRV 8825"]
  MJMP1 = Header 4 [package=jst-4-pth]
  MJP2 = Header 4 [package=jst-4-pth]
  Vin = Header 2 [package=screwterminal-3.5mm-2_lock]
  C2 = Electrolytic Capacitor [capacitance=100µF package="200 mil [THT, electrolytic]"]
  C3 = Electrolytic Capacitor [capacitance=100µF package="200 mil [THT, electrolytic]"]
  GYRO = MPU-6050 Board GY-521 [form="♀ (female)" package=THT]
  Balancebot_by_Gbaihd = Arduino Uno (Rev3)

nets:
  N1: DRV_1.MS1, DRV_2.MS1
  N2: DRV_1.MS2, DRV_2.MS2
  N3: DRV_1.MS3, DRV_2.MS3
  N4: DRV_1.RESET, DRV_1.SLEEP, DRV_2.RESET, DRV_2.SLEEP, C2.+, GYRO.pin1, Balancebot_by_Gbaihd.5V
  N5: DRV_1.STEP, DRV_2.STEP, Balancebot_by_Gbaihd.D3_PWM
  N6: DRV_1.DIRECTION, DRV_2.DIRECTION, Balancebot_by_Gbaihd.D4
  N7: DRV_1.VOLTAGE_ST/_MT, DRV_2.VOLTAGE_ST/_MT, Vin.1, C3.+, Balancebot_by_Gbaihd.VIN
  N8: DRV_1.GROUND_ST/_MT, DRV_1.GROUND_LOG, DRV_2.GROUND_ST/_MT, DRV_2.GROUND_LOG, Vin.2, C2.-, C3.-, GYRO.pin2, Balancebot_by_Gbaihd.GND
  N9: DRV_1.OUT_2B, MJMP1.1
  N10: DRV_1.OUT_2A, MJMP1.2
  N11: DRV_1.OUT_1A, MJMP1.3
  N12: DRV_1.OUT_1B, MJMP1.4
  N13: DRV_2.OUT_2B, MJP2.1
  N14: DRV_2.OUT_2A, MJP2.2
  N15: DRV_2.OUT_1A, MJP2.3
  N16: DRV_2.OUT_1B, MJP2.4
  N17: GYRO.pin3, Balancebot_by_Gbaihd.A5/SCL
  N18: GYRO.pin4, Balancebot_by_Gbaihd.A4/SDA
  N19: GYRO.pin5, Balancebot_by_Gbaihd.D2

custom parts:
  MPU-6050 Board GY-521: Acelerometro y Giroscopio MPU-6050 Board GY-521
